# Fritzing sketch Useless Box Schematic (saved by Fritzing 0.9.10b)
breadboards: 1

parts:
  Part1 = Arduino Uno (Rev3) - ICSP
  J1 = Basic Servo
  J2 = Basic Servo
  S1 = Toggle Switch [package=THT]
  R1 = Resistor [tolerance=±5% resistance=220 package="0402 [SMD]"]
  PART1 = APDS-9960 RGB and Gesture Sensor [part_number=SEN-12787]

nets:
  N1: Part1.A1, S1.L1, R1.Pin_1
  N2: Part1.A4/SDA, PART1.SDA
  N3: Part1.A5/SCL, PART1.SCL
  GND: Part1.GND, S1.COM, PART1.GND
  N4: Part1.D2, PART1.INT
  N5: Part1.D5_PWM, J2.pulse
  N6: Part1.D6_PWM, J1.pulse
  3V3: Part1.3V3, PART1.VCC
  N7: Part1.5V, R1.Pin_0
  GND_2: J1.gnd, J2.gnd
  VCC: J1.vcc, J2.vcc

custom parts:
  APDS-9960 RGB and Gesture Sensor: Breakout board for the Avago APDS-9960 proximity, light, RGB, and gesture sensors. Please visit www.sparkfun.com to learn more.
